# Fritzing sketch traffic_light_robot (saved by Fritzing 0.9.2b)
breadboards: 1

parts:
  Part1 = Arduino Uno (Rev3)
  R1 = Resistor [tolerance=±5% resistance=220 package=THT]
  R2 = Resistor [tolerance=±5% resistance=220 package=THT]
  R3 = Resistor [tolerance=±5% resistance=220 package=THT]
  S1 = Pushbutton [package="[THT]"]
  J1 = Piezo Speaker
  LED5 = LED - 5mm [color="Yellow (585nm)" package="5 mm [THT]"]
  LED6 = LED - 5mm [color="Red (633nm)" package="5 mm [THT]"]
  LED4 = LED - 5mm [color="Green (565nm)" package="5 mm [THT]"]
  R4 = Resistor [tolerance=±5% resistance=220 package=THT]
  R5 = Resistor [tolerance=±5% resistance=10k package=THT]

nets:
  N1: Part1.D11_PWM/MOSI, R1.Pin_0
  N2: Part1.D12/MISO, R2.Pin_0
  N3: Part1.D13/SCK, R3.Pin_0
  N4: Part1.D2, S1.Pin_3, S1.Pin_4, R5.Pin_0
  N5: Part1.D3_PWM, R4.Pin_1
  N6: Part1.5V, S1.Pin_1, S1.Pin_2
  N7: Part1.GND, J1.pin1, LED5.cathode, LED6.cathode, LED4.cathode, R5.Pin_1
  N8: R1.Pin_1, LED4.anode
  N9: R2.Pin_1, LED5.anode
  N10: R3.Pin_1, LED6.anode
  N11: J1.pin2, R4.Pin_0
